// Logisim project ARITHMETIC.circ as structural Verilog: 1 circuit, main circuit main
// S
module main (
  input  in_1,
  input  in_2,
  input  [1:0] SELECT,
  input  [1:0] A,
  input  [1:0] B,
  input  in_6,
  output D0,
  output D1,
  output out_9
);

  wire adder_1_cout, multiplexer_1_out, multiplexer_2_out, not_1_out, not_2_out, not_3_out;

  not not_1 (not_1_out, in_6);
  Multiplexer #(.select(2)) multiplexer_1 (
    .in0(B[1]), .in1(not_3_out), .in2(in_6), .in3(not_1_out), .out(multiplexer_1_out), .sel(SELECT), .en(in_2));
  not not_2 (not_2_out, B[0]);
  Multiplexer #(.select(2)) multiplexer_2 (
    .in0(B[0]), .in1(not_2_out), .in2(in_6), .in3(not_1_out), .out(multiplexer_2_out), .sel(SELECT), .en(in_2));
  not not_3 (not_3_out, B[1]);
  Adder #(.width(1)) adder_1 (.a(A[0]), .b(multiplexer_2_out), .out(D0), .cin(in_1), .cout(adder_1_cout));
  Adder #(.width(1)) adder_2 (.a(A[1]), .b(multiplexer_1_out), .out(D1), .cin(adder_1_cout), .cout(out_9));
endmodule
