// Logisim project FETCH AND DECODE ALL OPS.circ as structural Verilog: 1 circuit, main circuit main
module main (
);

  wire AC, and_6_out, and_7_out, and_8_out, clock_1_out, CLR, D4T4, D7_prime_T3I, d_ff_1_q, decoder_1_out0,
       decoder_1_out1, decoder_1_out2, decoder_1_out3, decoder_1_out4, decoder_1_out5, decoder_1_out6,
       decoder_1_out7, decoder_2_out0, decoder_2_out1, decoder_2_out4, decoder_2_out7, DR, FGI_q, not_1_out,
       or_1_out, or_2_out, PC;
  wire [2:0] S0_out, SC_q, selection;
  wire [11:0] AR_q, bit_extender_1_out, bit_extender_2_out, PC_q;
  wire [15:0] AC_q, adder_1_out, and_1_out, bit_extender_3_out, bit_extender_4_out, bit_extender_5_out, DR_q,
       IR_q, multiplexer_1_out, multiplexer_2_out, ram_1_data;

  Decoder #(.select(3)) decoder_1 (
    .out0(decoder_1_out0), .out1(decoder_1_out1), .out2(decoder_1_out2), .out3(decoder_1_out3),
    .out4(decoder_1_out4), .out5(decoder_1_out5), .out6(decoder_1_out6), .out7(decoder_1_out7), .sel(SC_q));  // open: en
  Counter #(.width(3), .max('h7)) SC (.Q(SC_q), .clk(clock_1_out), .clr(d_ff_1_q));  // open: load, D, count, carry
  D_Flip_Flop d_ff_1 (.clk(clock_1_out), .D(CLR), .Q(d_ff_1_q));  // open: Qn, preset, en, reset
  Clock clock_1 (.out(clock_1_out));
  or or_1 (or_1_out, decoder_1_out0, decoder_1_out2, D7_prime_T3I);
  Bit_Extender #(.in_width(16), .out_width(12)) bit_extender_1 (.in(multiplexer_2_out), .out(bit_extender_1_out));
  Bit_Extender #(.in_width(16), .out_width(12)) bit_extender_2 (.in(multiplexer_2_out), .out(bit_extender_2_out));
  Register #(.width(12)) AR (.D(bit_extender_1_out), .en(or_1_out), .Q(AR_q), .clk(clock_1_out));  // open: clr
  Counter #(.width(12), .max('hfff)) u_PC (
    .load(D4T4), .D(bit_extender_2_out), .count(PC), .Q(PC_q), .clk(clock_1_out));  // open: carry, clr
  Register #(.width(16)) IR (
    .D(multiplexer_2_out), .en(decoder_1_out1), .Q({IR_q[15], selection, IR_q[11:0]}), .clk(clock_1_out));  // open: clr
  Register #(.width(16)) u_AC (.D(multiplexer_1_out), .en(AC), .Q(AC_q), .clk(clock_1_out));  // open: clr
  Register #(.width(16)) u_DR (.D(multiplexer_2_out), .en(DR), .Q(DR_q), .clk(clock_1_out));  // open: clr
  RAM #(.addrWidth(12), .dataWidth(16)) ram_1 (
    .addr(AR_q), .data(ram_1_data), .clk(clock_1_out));  // open: sel, ld, clr
  assign bit_extender_3_out = {{4{1'b0}}, AR_q};  // Bit_Extender bit_extender_3
  assign bit_extender_4_out = {{4{1'b0}}, PC_q};  // Bit_Extender bit_extender_4
  assign and_1_out = AC_q & DR_q;  // AND_Gate and_1, 16 bits wide
  Adder #(.width(16)) adder_1 (.a(AC_q), .b(DR_q), .out(adder_1_out));  // open: cin, cout
  Multiplexer #(.select(3), .width(16)) multiplexer_1 (
    .in0(and_1_out), .in1(adder_1_out), .out(multiplexer_1_out), .sel(selection));  // open: in2, in3, in4, in5, in6, in7, en
  or S0 (S0_out[0], decoder_1_out1, DR, D4T4, and_7_out);
  or S1 (S0_out[1], decoder_1_out0, decoder_1_out1, DR);
  or S2 (S0_out[2], decoder_1_out1, DR, and_7_out);
  Multiplexer #(.select(3), .width(16)) multiplexer_2 (
    .in1(bit_extender_3_out), .in2(bit_extender_4_out), .in3(DR_q), .in4(AC_q), .in5(bit_extender_5_out),
    .in7(ram_1_data), .out(multiplexer_2_out), .sel(S0_out));  // open: in0, in6, en
  assign bit_extender_5_out = {{4{1'b0}}, IR_q[11:0]};  // Bit_Extender bit_extender_5
  or or_2 (or_2_out, decoder_2_out0, decoder_2_out1);
  Decoder #(.select(3)) decoder_2 (
    .out0(decoder_2_out0), .out1(decoder_2_out1), .out4(decoder_2_out4), .out7(decoder_2_out7),
    .sel(selection));  // open: out2, out3, out5, out6, en
  not not_1 (not_1_out, decoder_2_out7);
  and and_2 (AC, decoder_1_out5, or_2_out);
  and and_3 (DR, or_2_out, decoder_1_out4);
  and and_4 (D4T4, decoder_1_out4, decoder_2_out4);
  and and_5 (D7_prime_T3I, decoder_1_out3, not_1_out, IR_q[15]);
  and and_6 (and_6_out, IR_q[9], decoder_1_out3, IR_q[15], decoder_2_out7);
  D_Flip_Flop FGI (.clk(clock_1_out), .Q(FGI_q));  // open: D, Qn, preset, en, reset
  and and_7 (and_7_out, decoder_1_out2, decoder_2_out4);
  or or_3 (CLR, AC, D4T4);
  or or_4 (PC, decoder_1_out1, and_8_out);
  and and_8 (and_8_out, and_6_out, FGI_q);
endmodule
