// Logisim project associativememory128.circ as structural Verilog: 1 circuit, main circuit main
module main (
  input  in_1,
  output [3:0] out_2,
  output out_3
);

  wire and_1_out, and_2_out, and_3_out, and_5_out, ARGUMENT_q0, ARGUMENT_q1, ARGUMENT_q2, ARGUMENT_q3, clk,
       k0, k1, k2, k3, not_1_out, not_2_out, not_3_out, not_4_out, not_5_out, not_6_out, not_7_out,
       not_8_out, or_1_out, or_2_out, or_3_out, or_4_out, x0, x1, x1_2_out, x1_3_out, x1_4_out, x1_5_out,
       x1_6_out, x1_7_out, x1_8_out, x1_out, x2, x3;
  wire [3:0] counter_1_q;

  Counter #(.width(4), .max('hf)) counter_1 (.Q(counter_1_q), .clk(clk));  // open: load, D, count, carry, clr
  Shift_Register #(.length(4)) KEY (
    .q0(k3), .q1(k2), .q2(k1), .q3(k0));  // open: shift, in, clk, out, load, clr, d0, d1, d2, d3
  Clock u_CLK (.out(clk));
  RAM #(.addrWidth(4), .dataWidth(4), .bus("separate")) ram_1 (
    .addr(counter_1_q), .data(out_2), .clk(clk), .ld(in_1));  // open: din, str, sel, clr
  not not_1 (not_1_out, k0);
  not not_2 (not_2_out, k1);
  not not_3 (not_3_out, k2);
  not not_4 (not_4_out, k3);
  Shift_Register #(.length(4)) ARGUMENT (
    .q0(ARGUMENT_q0), .q1(ARGUMENT_q1), .q2(ARGUMENT_q2), .q3(ARGUMENT_q3));  // open: shift, in, clk, out, load, clr, d0, d1, d2, d3
  or or_1 (or_1_out, not_1_out, x0);
  or or_2 (or_2_out, not_2_out, x1);
  or or_3 (or_3_out, not_3_out, x2);
  or or_4 (or_4_out, not_4_out, x3);
  not not_5 (not_5_out, ARGUMENT_q0);
  not not_6 (not_6_out, out_2[3]);
  not not_7 (not_7_out, ARGUMENT_q3);
  not not_8 (not_8_out, out_2[0]);
  not u_x1 (x1_out, ARGUMENT_q2);
  not x1_2 (x1_2_out, out_2[1]);
  not x1_3 (x1_3_out, ARGUMENT_q1);
  and x1_4 (x1_4_out, ARGUMENT_q1, out_2[2]);
  not x1_5 (x1_5_out, out_2[2]);
  and and_1 (and_1_out, ARGUMENT_q0, out_2[3]);
  and and_2 (and_2_out, ARGUMENT_q3, out_2[0]);
  and x1_6 (x1_6_out, ARGUMENT_q2, out_2[1]);
  and and_3 (and_3_out, not_5_out, not_6_out);
  and and_4 (out_3, or_1_out, or_2_out, or_3_out, or_4_out);
  and and_5 (and_5_out, not_7_out, not_8_out);
  and x1_7 (x1_7_out, x1_out, x1_2_out);
  and x1_8 (x1_8_out, x1_3_out, x1_5_out);
  or x1_9 (x2, x1_4_out, x1_8_out);
  or or_5 (x3, and_1_out, and_3_out);
  or or_6 (x0, and_2_out, and_5_out);
  or x1_10 (x1, x1_6_out, x1_7_out);
endmodule
