// Logisim project booth128.circ as structural Verilog: 1 circuit, main circuit main
module main (
  input  in_1,
  input  in_2,
  output [3:0] out_3,
  output [3:0] out_4,
  output [3:0] out_5
);

  wire ASHR, d_ff_1_q, not_1_out, not_2_out, not_4_out, xor_5_out;
  wire [3:0] A0, B0, B1, B2, B3, shift_register_1_out, shift_register_1_q0, shift_register_1_q1,
       shift_register_1_q2, shift_register_2_out, shift_register_2_q0;
  wire [3:2] adder_1_out;
  wire [3:3] c0;

  Shift_Register #(.width(4), .length(4)) shift_register_1 (
    .clk(in_1), .out(shift_register_1_out), .q0(shift_register_1_q0), .q1(shift_register_1_q1),
    .q2(shift_register_1_q2));  // open: shift, in, load, clr, d0, d1, d2, d3, q3
  Shift_Register #(.width(4), .length(4)) shift_register_2 (
    .in(A0), .clk(in_1), .out(shift_register_2_out), .q0(shift_register_2_q0));  // open: shift, load, clr, d0, d1, q1, d2, q2, d3, q3
  not not_1 (not_1_out, d_ff_1_q);
  not not_2 (not_2_out, ASHR);
  D_Flip_Flop d_ff_1 (.clk(in_1), .D(shift_register_2_out[0]), .Q(d_ff_1_q));  // open: Qn, preset, en, reset
  xor xor_1 (out_3[0], not_1_out, shift_register_1_out[0]);
  xor xor_2 (out_3[1], not_1_out, shift_register_1_q2[0]);
  xor xor_3 (out_3[2], not_1_out, shift_register_1_q1[0]);
  xor xor_4 (out_3[3], not_1_out, shift_register_1_q0[0]);
  xor xor_5 (xor_5_out, d_ff_1_q, shift_register_2_out[0]);
  not not_3 (ASHR, xor_5_out);
  not not_4 (not_4_out, ASHR);
  Shift_Register #(.width(4), .length(4)) shift_register_3 (
    .clk(not_4_out), .out(out_4), .q0(B0), .q1(B1), .q2(B2), .q3(B3));  // open: shift, in, load, clr, d0, d1, d2, d3
  Shift_Register #(.width(4), .length(4)) shift_register_4 (
    .clk(not_2_out), .d0({c0[3], {3{in_2}}}), .d1({out_5[3:2], out_5[2], out_5[0]}));  // open: shift, in, out, load, clr, q0, q1, d2, q2, d3, q3
  Adder #(.width(4)) adder_1 (
    .a(out_3), .b(out_4), .out({adder_1_out, out_5[0], c0[3]}), .cin(not_1_out));  // open: cout

  assign out_5[1] = out_5[2];

  // Other names for the same wires on the sheet: c0[2:0] = {3{in_2}}; c1[3:0] = {out_5[3:2], out_5[2], out_5[0]};
  //   clock = in_1
endmodule
