// Logisim project bus.circ as structural Verilog: 1 circuit, main circuit main
module main (
  input  in_1,
  input  [1:0] in_2,
  input  in_3,
  input  in_4,
  input  in_5
);

  wire multiplexer_1_out, multiplexer_2_out, multiplexer_3_out, shift_register_1_q0, shift_register_1_q1,
       shift_register_1_q2, shift_register_1_q3, shift_register_3_q0, shift_register_3_q1,
       shift_register_3_q2, shift_register_3_q3, shift_register_4_q0, shift_register_4_q1,
       shift_register_4_q2, shift_register_4_q3, shift_register_5_q0, shift_register_5_q1,
       shift_register_5_q2, shift_register_5_q3, undriven;

  Shift_Register #(.length(4)) shift_register_1 (
    .in(in_4), .clk(in_5), .q0(shift_register_1_q0), .q1(shift_register_1_q1), .q2(shift_register_1_q2),
    .q3(shift_register_1_q3));  // open: shift, out, load, clr, d0, d1, d2, d3
  Multiplexer #(.select(2)) multiplexer_1 (
    .in0(shift_register_1_q0), .in1(shift_register_3_q0), .in2(shift_register_4_q0),
    .in3(shift_register_5_q0), .out(multiplexer_1_out), .sel(in_2), .en(in_3));
  Shift_Register #(.length(4)) shift_register_2 (
    .clk(in_5), .load(in_1), .d0(multiplexer_1_out), .d1(multiplexer_2_out), .d2(multiplexer_3_out),
    .d3(undriven));  // open: shift, in, out, clr, q0, q1, q2, q3
  Shift_Register #(.length(4)) shift_register_3 (
    .clk(in_5), .q0(shift_register_3_q0), .q1(shift_register_3_q1), .q2(shift_register_3_q2),
    .q3(shift_register_3_q3));  // open: shift, in, out, load, clr, d0, d1, d2, d3
  Multiplexer #(.select(2)) multiplexer_2 (
    .in0(shift_register_1_q1), .in1(shift_register_3_q1), .in2(shift_register_4_q1),
    .in3(shift_register_5_q1), .out(multiplexer_2_out), .sel(in_2), .en(in_3));
  Shift_Register #(.length(4)) shift_register_4 (
    .clk(in_5), .q0(shift_register_4_q0), .q1(shift_register_4_q1), .q2(shift_register_4_q2),
    .q3(shift_register_4_q3));  // open: shift, in, out, load, clr, d0, d1, d2, d3
  Multiplexer #(.select(2)) multiplexer_3 (
    .in0(shift_register_1_q2), .in1(shift_register_3_q2), .in2(shift_register_4_q2),
    .in3(shift_register_5_q2), .out(multiplexer_3_out), .sel(in_2), .en(in_3));
  Shift_Register #(.length(4)) shift_register_5 (
    .clk(in_5), .q0(shift_register_5_q0), .q1(shift_register_5_q1), .q2(shift_register_5_q2),
    .q3(shift_register_5_q3));  // open: shift, in, out, load, clr, d0, d1, d2, d3
  Multiplexer #(.select(2)) multiplexer_4 (
    .in1(shift_register_1_q3), .in2(shift_register_3_q3), .in3(shift_register_4_q3), .sel(in_2), .en(in_3));  // open: in0, out
endmodule
