// Logisim project division.circ as structural Verilog: 1 circuit, main circuit main
module main (
  output out_1,
  output [4:0] out_2,
  output [4:0] out_3
);

  wire A_out, CLOCK, Q_q0, UP_E;
  wire [2:0] SC;
  wire [4:0] A, B, multiplexer_1_out;

  Clock clock_1 (.out(CLOCK));
  Shift_Register #(.length(5)) Q (.q0(Q_q0));  // open: shift, in, clk, out, load, clr, d0, d1, q1, d2, q2, d3, q3, d4, q4
  Shift_Register #(.length(5)) shift_register_1 (
    .q0(B[4]), .q1(B[3]), .q2(B[2]), .q3(B[1]), .q4(B[0]));  // open: shift, in, clk, out, load, clr, d0, d1, d2, d3, d4
  Counter #(.width(3), .max('h7)) counter_1 (
    .load(1'b1), .D(SC), .count(1'b1), .Q(SC), .clk(CLOCK));  // open: carry, clr
  Shift_Register #(.length(5)) u_A (
    .clk(CLOCK), .out(A_out), .load(1'b1), .d0(A[3]), .q0(A[4]), .d1(A[2]), .q1(A[3]), .d2(A[1]), .q2(A[2]),
    .d3(A[0]), .q3(A[1]), .d4(Q_q0), .q4(A[0]));  // open: shift, in, clr
  xor xor_1 (out_3[4], B[4], 1'b1);
  xor xor_2 (out_3[3], B[3], 1'b1);
  xor xor_3 (out_3[2], B[2], 1'b1);
  xor xor_4 (out_3[1], B[1], 1'b1);
  xor xor_5 (out_3[0], B[0], 1'b1);
  D_Flip_Flop d_ff_1 (.clk(CLOCK), .D(A[4]), .Q(UP_E));  // open: Qn, preset, en, reset
  xor xor_6 (out_1, A[0], B[0]);
  Multiplexer #(.width(5)) multiplexer_1 (.in0(out_3), .in1(B), .out(multiplexer_1_out), .sel(A[4]));  // open: en
  Adder #(.width(5)) adder_1 (.a(A), .b(multiplexer_1_out), .out(out_2), .cin(1'b1));  // open: cout
  Register #(.width(5)) register_1 (.D(out_2), .clk(CLOCK));  // open: en, Q, clr

  // Other names for the same wires on the sheet: E = A[4]; As_XOR_Bs = out_1; B_prime[4:0] = out_3
endmodule
