// Logisim project fetchcyclefinal.circ as structural Verilog: 2 circuits, main circuit main
module main (
  input  in_1,
  output [15:0] out_2
);

  wire clock, decoder_1_out0, decoder_1_out1, decoder_1_out2;
  wire [2:0] or_1_out;
  wire [3:0] counter_1_q;
  wire [11:0] bit_extender_1_out, bit_extender_2_out, PC_q, register_1_q;
  wire [15:0] bit_extender_3_out, bit_extender_4_out, multiplexer_1_out, ram_1_data;

  Clock clock_1 (.out(clock));
  Counter #(.width(4), .max('hf)) counter_1 (
    .Q(counter_1_q), .clk(clock), .clr(decoder_1_out2));  // open: load, D, count, carry
  Decoder #(.select(4)) decoder_1 (
    .out0(decoder_1_out0), .out1(decoder_1_out1), .out2(decoder_1_out2), .sel(counter_1_q));  // open: out3, out4, out5, out6, out7, out8, out9, out10, out11, out12, out13, out14, out15, en
  Bit_Extender #(.in_width(16), .out_width(12)) bit_extender_1 (.in(multiplexer_1_out), .out(bit_extender_1_out));
  Bit_Extender #(.in_width(16), .out_width(12)) bit_extender_2 (.in(multiplexer_1_out), .out(bit_extender_2_out));
  buf or_1 (or_1_out[0], decoder_1_out1);  // OR_Gate
  or or_2 (or_1_out[1], decoder_1_out1, decoder_1_out0, decoder_1_out1);
  buf or_3 (or_1_out[2], decoder_1_out1);  // OR_Gate
  Register #(.width(12)) register_1 (
    .D(bit_extender_1_out), .en(decoder_1_out0), .Q(register_1_q), .clk(clock));  // open: clr
  Counter #(.width(12), .max('hfff)) PC (
    .D(bit_extender_2_out), .count(decoder_1_out1), .Q(PC_q), .clk(clock));  // open: load, carry, clr
  Register #(.width(16)) register_2 (.D(multiplexer_1_out), .en(decoder_1_out1), .Q(out_2), .clk(clock));  // open: clr
  Register register_3 ();  // open: D, en, Q, clk, clr
  RAM #(.addrWidth(12), .dataWidth(16)) ram_1 (.addr(register_1_q), .data(ram_1_data));  // open: sel, clk, ld, clr
  assign bit_extender_3_out = {{4{1'b0}}, register_1_q};  // Bit_Extender bit_extender_3
  assign bit_extender_4_out = {{4{1'b0}}, PC_q};  // Bit_Extender bit_extender_4
  Multiplexer #(.select(3), .width(16)) multiplexer_1 (
    .in1(bit_extender_3_out), .in2(bit_extender_4_out), .in5(out_2), .in7(ram_1_data),
    .out(multiplexer_1_out), .sel(or_1_out), .en(in_1));  // open: in0, in3, in4, in6
endmodule

module _12_16bit (
  input  [11:0] in_1,
  input  in_2,
  output [15:0] out_3
);


  assign out_3 = {{4{in_2}}, in_1};
endmodule
