// Logisim project fetchcyclefinalOPERATION.circ as structural Verilog: 2 circuits, main circuit main
module main (
  input  in_1,
  input  in_2,
  input  in_3
);

  wire and_2_out, clock, decoder_1_out0, decoder_1_out1, decoder_1_out2, decoder_1_out4, decoder_1_out6,
       decoder_2_out0, decoder_2_out1;
  wire [2:0] IR_q_2, or_2_out;
  wire [3:0] counter_1_q;
  wire [11:0] AR_q, bit_extender_1_out, bit_extender_2_out, IR_q, multiplexer_1_out, PC_q;
  wire [15:0] AC_q, and_1_out, bit_extender_3_out, bit_extender_4_out, DR_q, multiplexer_2_out, ram_1_data,
       undriven;
  wire [15:15] IR_q_3;

  Clock clock_1 (.out(clock));
  Counter #(.width(4), .max('hf)) counter_1 (
    .Q(counter_1_q), .clk(clock), .clr(decoder_1_out6));  // open: load, D, count, carry
  Decoder #(.select(4)) decoder_1 (
    .out0(decoder_1_out0), .out1(decoder_1_out1), .out2(decoder_1_out2), .out4(decoder_1_out4),
    .out6(decoder_1_out6), .sel(counter_1_q));  // open: out3, out5, out7, out8, out9, out10, out11, out12, out13, out14, out15, en
  // OR_Gate or_1 has open pins: in1=undriven, out=open
  Bit_Extender #(.in_width(16), .out_width(12)) bit_extender_1 (.in(multiplexer_2_out), .out(bit_extender_1_out));
  Bit_Extender #(.in_width(16), .out_width(12)) bit_extender_2 (.in(multiplexer_2_out), .out(bit_extender_2_out));
  Register #(.width(16)) DR (.D(ram_1_data), .Q(DR_q), .clk(in_3));  // open: en, clr
  Register #(.width(16)) AC (.D(and_1_out), .Q(AC_q), .clk(and_2_out));  // open: en, clr
  buf or_2 (or_2_out[0], decoder_1_out1);  // OR_Gate
  or or_3 (or_2_out[1], decoder_1_out1, decoder_1_out0, decoder_1_out1);
  buf or_4 (or_2_out[2], decoder_1_out1);  // OR_Gate
  Multiplexer #(.width(12)) multiplexer_1 (
    .in0(AR_q), .in1(IR_q), .out(multiplexer_1_out), .sel(decoder_1_out0), .en(in_2));
  Register #(.width(12)) AR (.D(bit_extender_1_out), .en(decoder_1_out0), .Q(AR_q), .clk(clock));  // open: clr
  Counter #(.width(12), .max('hfff)) PC (
    .D(bit_extender_2_out), .count(decoder_1_out1), .Q(PC_q), .clk(clock));  // open: load, carry, clr
  Register #(.width(16)) IR (
    .D(multiplexer_2_out), .en(decoder_1_out1), .Q({IR_q_3[15], IR_q_2, IR_q}), .clk(clock));  // open: clr
  assign and_1_out = DR_q & AC_q;  // AND_Gate and_1, 16 bits wide
  Register register_1 ();  // open: D, en, Q, clk, clr
  assign bit_extender_3_out = {{4{1'b0}}, AR_q};  // Bit_Extender bit_extender_3
  assign bit_extender_4_out = {{4{1'b0}}, PC_q};  // Bit_Extender bit_extender_4
  RAM #(.addrWidth(12), .dataWidth(16)) ram_1 (.addr(multiplexer_1_out), .data(ram_1_data));  // open: sel, clk, ld, clr
  Decoder #(.select(3)) decoder_2 (
    .out0(decoder_2_out0), .out1(decoder_2_out1), .sel(IR_q_2));  // open: out2, out3, out4, out5, out6, out7, en
  and and_2 (and_2_out, decoder_1_out4, decoder_2_out0);
  Multiplexer #(.select(3), .width(16)) multiplexer_2 (
    .in1(bit_extender_3_out), .in2(bit_extender_4_out), .in5({IR_q_3[15], IR_q_2, IR_q}), .in7(ram_1_data),
    .out(multiplexer_2_out), .sel(or_2_out), .en(in_1));  // open: in0, in3, in4, in6
endmodule

module _12_16bit (
  input  [11:0] in_1,
  input  in_2,
  output [15:0] out_3
);


  assign out_3 = {{4{in_2}}, in_1};
endmodule
