// Logisim project fullADDERSHIFT.circ as structural Verilog: 1 circuit, main circuit main
module main (
  input  in_1,
  input  in_2,
  output out_3,
  output out_4
);

  wire adder_1_cout, clock_1_out, shift_register_1_out, shift_register_2_out;

  Clock clock_1 (.out(clock_1_out));
  Shift_Register #(.length(4)) shift_register_1 (
    .shift(in_1), .in(out_3), .clk(clock_1_out), .out(shift_register_1_out));  // open: load, clr, d0, q0, d1, q1, d2, q2, d3, q3
  Shift_Register #(.length(4)) shift_register_2 (
    .shift(in_1), .in(in_2), .clk(clock_1_out), .out(shift_register_2_out));  // open: load, clr, d0, q0, d1, q1, d2, q2, d3, q3
  Adder #(.width(1)) adder_1 (
    .a(shift_register_1_out), .b(shift_register_2_out), .out(out_3), .cin(out_4), .cout(adder_1_cout));
  D_Flip_Flop d_ff_1 (.clk(clock_1_out), .D(adder_1_cout), .Q(out_4));  // open: Qn, preset, en, reset
endmodule
