// Logisim project logical.circ as structural Verilog: 1 circuit, main circuit main
module main (
  input  [1:0] in_1,
  input  [1:0] in_2,
  input  in_3,
  input  [1:0] in_4,
  input  in_5,
  output out_6,
  output out_7
);

  wire and_1_out, and_2_out, not_1_out, not_2_out, or_1_out, or_2_out, xor_1_out, xor_2_out;

  and and_1 (and_1_out, in_1[0], in_4[0]);
  or or_1 (or_1_out, in_1[0], in_4[0]);
  xor xor_1 (xor_1_out, in_1[0], in_4[0]);
  not not_1 (not_1_out, in_1[0]);
  and and_2 (and_2_out, in_1[1], in_4[1]);
  not not_2 (not_2_out, in_1[1]);
  Multiplexer #(.select(2)) multiplexer_1 (
    .in0(and_1_out), .in1(or_1_out), .in2(xor_1_out), .in3(not_1_out), .out(out_6), .sel(in_2), .en(in_3));
  or or_2 (or_2_out, in_1[1], in_4[1]);
  xor xor_2 (xor_2_out, in_1[1], in_4[1]);
  Multiplexer #(.select(2)) multiplexer_2 (
    .in0(and_2_out), .in1(or_2_out), .in2(xor_2_out), .in3(not_2_out), .out(out_7), .sel(in_2), .en(in_5));
endmodule
