// Logisim project priority encoder.circ as structural Verilog: 1 circuit, main circuit main
module main (
  input  [3:0] in_1,
  output out_2,
  output out_3,
  output out_4
);

  wire and_1_out, and_2_out, not_1_out, not_2_out, not_3_out;

  not not_1 (not_1_out, in_1[0]);
  not not_2 (not_2_out, in_1[1]);
  not not_3 (not_3_out, in_1[2]);
  and and_1 (and_1_out, not_1_out, in_1[1]);
  and and_2 (and_2_out, not_1_out, not_3_out);
  or or_1 (out_4, in_1[0], in_1[1], in_1[3]);
  and and_3 (out_2, not_1_out, not_2_out);
  or or_2 (out_3, and_1_out, and_2_out);
endmodule
