// Logisim project push and pop.circ as structural Verilog: 1 circuit, main circuit main
module main (
  input  in_1,
  input  [1:0] in_2,
  input  [1:0] in_3,
  output [11:0] out_4,
  output [1:0] out_5,
  output [1:0] out_6
);

  wire CLOCK, POP;
  wire [1:0] VALUE;
  wire [15:0] ram_1_data, register_1_q;

  Clock clock_1 (.out(CLOCK));
  not not_1 (POP, in_1);
  RAM #(.addrWidth(12), .dataWidth(16), .bus("separate")) ram_1 (
    .addr(out_4), .din(register_1_q), .data(ram_1_data), .str(in_1), .clk(CLOCK), .ld(POP));  // open: sel, clr
  Counter #(.width(12), .max('hfff)) SP (.load(POP), .count(1'b1), .Q(out_4), .clk(CLOCK));  // open: D, carry, clr
  Counter #(.width(2), .max('h3)) counter_1 (
    .load(POP), .D(VALUE), .count(1'b1), .Q(VALUE), .clk(CLOCK));  // open: carry, clr
  Register #(.width(16)) register_1 (.D(ram_1_data), .en(POP), .Q(register_1_q), .clk(CLOCK));  // open: clr
  assign out_5 = VALUE ^ in_2;  // XOR_Gate xor_1, 2 bits wide
  assign out_6 = VALUE ^ in_3;  // XOR_Gate xor_2, 2 bits wide

  // Other names for the same wires on the sheet: PUSH = in_1; SP[11:0] = out_4
endmodule
